# Fritzing sketch temp_monitoring&datalogger_project (saved by Fritzing 0.9.3b)

parts:
  U1 = NodeMCU V3.0
  Part1 = Bluetooth HC-05 Macho
  Mod1 = gy-906
  U2 = LIPO-1000mAh [package=lipo-1000]

nets:
  N1: U1.D1, Mod1.SDA
  N2: U1.D2, Mod1.SCL
  N3: U1.D3, Part1.TXD
  N4: U1.D4, Part1.RXD
  GND: U1.GND, Part1.GND, Mod1.GND, U2.-
  3V3: U1.3V3, Part1.VCC, Mod1.VIN
  N5: U1.Vin, U2.+

custom parts:
  NodeMCU V3.0: NodeMcu V3 Lua WIFI Development Board
  gy-906: gy-906 Non-contact PIR I2C interface temperature sensor breakout board.
